# Fritzing sketch Console Wireing (saved by Fritzing 1.0.2b)
breadboards: 1

parts:
  A6 = Arduino UNO R4 WiFi
  Part1 = Thumb Joystick
  Grove1 = Grove OLED 128x96

nets:
  VCC: A6.Pin_8, A6.Pin_27, Part1.VCC, Grove1.VCC
  GND: A6.Pin_10, A6.Pin_48, Part1.GND, Grove1.GND
  N1: A6.Pin_13, Part1.VERT
  N2: A6.Pin_36, Part1.SEL
  N3: A6.Pin_50, Grove1.SDA
  N4: A6.Pin_51, Grove1.SCL

custom parts:
  Arduino UNO R4 WiFi: The Arduino UNO R4 WiFi merges the RA4M1 microprocessor from Renesas with the ESP32-S3 from Espressif, creating an all-in-one tool for makers with enhanced processing power and a diverse array of new peripherals.
